# Fritzing sketch buttons_and_led_matrix (saved by Fritzing 0.9.3b)
breadboards: 2

parts:
  Part1 = Adafruit Metro M0 Express
  S10 = Pushbutton [package="[THT]"]
  S9 = Pushbutton [package="[THT]"]
  S8 = Pushbutton [package="[THT]"]
  S7 = Pushbutton [package="[THT]"]
  S6 = Pushbutton [package="[THT]"]
  S4 = Pushbutton [package="[THT]"]
  S3 = Pushbutton [package="[THT]"]
  S5 = Pushbutton [package="[THT]"]
  S2 = Pushbutton [package="[THT]"]
  S1 = Pushbutton [package="[THT]"]
  R1 = Resistor [tolerance=±5% resistance=220 package=THT]
  U1 = 74HC595 SMD [package="SO16 [SMD]"]
  U2 = 74HC595 SMD [package="SO16 [SMD]"]
  LED6 = LED - 5mm [color="Red (633nm)" package="5 mm [THT]"]
  LED5 = LED - 5mm [color="Red (633nm)" package="5 mm [THT]"]
  LED4 = LED - 5mm [color="Red (633nm)" package="5 mm [THT]"]
  LED13 = LED - 5mm [color="Red (633nm)" package="5 mm [THT]"]
  LED1 = LED - 5mm [color="Red (633nm)" package="5 mm [THT]"]
  LED6_2 = LED - 5mm [color="Red (633nm)" package="5 mm [THT]"]
  LED18 = LED - 5mm [color="Red (633nm)" package="5 mm [THT]"]
  LED15 = LED - 5mm [color="Red (633nm)" package="5 mm [THT]"]
  LED10 = LED - 5mm [color="Red (633nm)" package="5 mm [THT]"]
  LED9 = LED - 5mm [color="Red (633nm)" package="5 mm [THT]"]

nets:
  N1: Part1.D13, S10.Pin_1, S10.Pin_2, S5.Pin_1, S5.Pin_2
  N2: Part1.D12, S9.Pin_1, S9.Pin_2, S4.Pin_1
  N3: Part1.D11, S8.Pin_1, S8.Pin_2, S3.Pin_1
  N4: Part1.D10, S7.Pin_1, S2.Pin_1
  N5: Part1.D9, S6.Pin_1, S6.Pin_2, S1.Pin_1, S1.Pin_2
  N6: Part1.D7, S10.Pin_3, S10.Pin_4, S9.Pin_3, S8.Pin_3, S8.Pin_4, S7.Pin_3, S6.Pin_3, S6.Pin_4
  N7: Part1.D6, S4.Pin_3, S4.Pin_4, S3.Pin_3, S5.Pin_3, S5.Pin_4, S2.Pin_3, S2.Pin_4, S1.Pin_3
  N8: Part1.D5, U1.ST_CP, U2.ST_CP
  N9: Part1.D4, U1.SH_CP, U2.SH_CP
  N10: Part1.D3, U1.DS
  N11: R1.Pin_0, U1.GND
  VCC: R1.Pin_1, U1.MR, U1.VCC, U2.MR, U2.OE, U2.VCC, LED6.cathode, LED5.cathode, LED4.cathode, LED13.cathode, LED1.cathode, LED1.anode, LED6_2.cathode, LED18.cathode, LED15.cathode, LED10.cathode, LED9.cathode
  N12: U1.Q1, LED13.anode
  N13: U1.Q2, LED6.anode
  N14: U1.Q3, LED4.anode
  N15: U1.Q4, LED5.anode
  N16: U1.Q5, LED6_2.anode
  N17: U1.Q7, LED15.anode
  N18: U1.Q7', U2.DS
  N19: U1.OE, U2.GND
  N20: U2.Q1, LED10.anode
  N21: U2.Q0, LED9.anode

custom parts:
  Adafruit Metro M0 Express: Metro is our series of microcontroller boards for use with the Arduino IDE. This new Metro board looks a whole lot like our original Metro 328, but with a huge upgrade. Instead of the ATmega328, this Metro features a ATSAMD21G18 chip, an ARM Cortex M0+. It's our first Metro that is designed for use with CircuitPython! CircuitPython is our beginner-oriented flavor of MicroPython - and as the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
